// Logisim project PONG74_Beta.circ as structural Verilog: 1 circuit, main circuit main
module main (
  input  in_1,
  input  in_2,
  input  in_3,
  input  in_4,
  input  in_5,
  input  in_6,
  input  in_7,
  input  in_8,
  input  in_9,
  input  in_10,
  input  in_11,
  input  in_12,
  input  in_13,
  input  in_14,
  input  in_15,
  input  in_16,
  input  in_17,
  input  in_18,
  input  in_19,
  input  in_20
);

  wire a, a1, aa, ab, ac, ad, ae, af, ag, ah, ai, aj, ak, al, am, an, and_1_out, and_2_out, and_11_out,
       and_12_out, and_21_out, and_22_out, and_23_out, and_24_out, and_25_out, and_26_out, and_27_out,
       and_28_out, and_47_out, and_48_out, and_49_out, ao, ap, aq, ar, as, at, au, av, aw, ax, ay, az, b, b1,
       ba, ballbit0, ballbit1, ballbit2, ballbit3, ballbit4, ballbit5, ballbit6, ballbit7, ballgodown,
       ballgoup, BallHitLeft, BallHitRight, bb, bc, bd, be, bf, bg, bh, bi, bj, bk, bl, bm, bn, bo, bp, bq,
       br, bs, bt, bu, bv, bw, bx, by, bz, c, c1, ca, cb, clock_1_out, clock_2_out, clock_3_out, Collision0,
       Collision1, Collision2, Collision3, Collision4, Collision5, Collision6, Collision7, CountDOWN0,
       CountDOWN1, CountDOWN2, CountDOWN3, CountDOWN4, CountDOWN5, CountDOWN6, CountDOWN7, CountOFF0,
       CountOFF1, CountOFF2, CountOFF3, CountOFF4, CountOFF5, CountOFF6, CountOFF7, CountUP0, CountUP1,
       CountUP2, CountUP3, CountUP4, CountUP5, CountUP6, CountUP7, d, d1, e, e1, END0, END1, END2, END3,
       END4, END5, END6, END7, f, f1, g, g1, GridInflictedChange, GridInflictedDOWN, GridInflictedUP,
       GUARANTEED_ENDGAME, h, h1, i, i1, j, j1, k, l, m, n, n74138_1_pin4, n74138_1_pin5, n74138_1_pin6,
       n74138_1_pin7, n74138_1_pin9, n74138_1_pin10, n74138_1_pin11, n74138_1_pin12, n74138_1_pin13,
       n74138_1_pin14, n74138_1_pin15, n74193_1_pin2, n74193_1_pin3, n74193_1_pin4, n74193_1_pin5,
       n74193_1_pin6, n74193_2_pin2, n74193_2_pin3, n74193_2_pin4, n74193_2_pin5, n74193_2_pin6,
       n74193_2_pin7, n74244_1_pin3, n74244_1_pin5, n74244_1_pin7, n74244_1_pin9, n74244_1_pin12,
       n74244_1_pin14, n74244_2_pin3, n74244_2_pin5, n74244_2_pin7, n74244_2_pin9, n74244_4_pin6,
       n74244_4_pin8, n74244_5_pin1, n74244_5_pin2, nor_1_out, nor_2_out, nor_3_out, nor_4_out, nor_5_out,
       nor_6_out, nor_7_out, nor_8_out, nor_11_out, not_11_out, not_12_out, not_13_out, not_14_out,
       not_15_out, not_16_out, not_17_out, not_18_out, not_22_out, not_23_out, not_24_out, not_25_out,
       not_26_out, not_27_out, not_28_out, not_29_out, not_33_out, not_34_out, not_35_out, not_37_out,
       not_38_out, not_39_out, not_40_out, not_41_out, not_42_out, not_43_out, not_44_out, not_45_out,
       not_46_out, not_47_out, not_48_out, not_49_out, not_50_out, not_51_out, not_52_out, not_53_out,
       not_54_out, not_55_out, not_56_out, not_57_out, not_58_out, not_59_out, not_60_out, not_61_out,
       not_62_out, not_63_out, not_64_out, not_65_out, not_66_out, not_67_out, not_68_out, not_69_out,
       not_70_out, not_71_out, not_72_out, not_73_out, not_74_out, not_75_out, not_76_out, not_77_out,
       not_78_out, not_79_out, not_80_out, not_81_out, not_82_out, not_83_out, not_84_out, not_85_out,
       not_86_out, not_87_out, not_88_out, not_89_out, not_90_out, not_91_out, not_92_out, not_93_out,
       not_94_out, not_95_out, not_96_out, not_97_out, not_98_out, not_99_out, not_100_out, not_101_out,
       not_102_out, not_103_out, not_104_out, not_105_out, not_106_out, not_107_out, not_108_out,
       not_109_out, not_110_out, not_111_out, not_112_out, not_113_out, not_114_out, not_115_out,
       not_116_out, o, p, P1_HIT, P2_HIT, PaddleBottom, PaddleInflictedChange, PaddleInflictedDOWN,
       PaddleInflictedOFF, PaddleInflictedUP, PaddleTop, q, r, s, t, u, unchecked_Collision,
       unchecked_countOFF, unchecked_countUP, unchecked_DOWN, unchecked_ENDGAME, v, w, x, xor_1_out,
       xor_2_out, xor_3_out, xor_4_out, xor_5_out, xor_6_out, xor_7_out, xor_8_out, xor_17_out, xor_18_out,
       y, z;

  Clock clock_1 (.out(clock_1_out));
  _74193 #(.ShowInternalStructure("true")) u_74193_1 (
    .pin2(n74193_1_pin2), .pin3(n74193_1_pin3), .pin4(n74193_1_pin4), .pin5(n74193_1_pin5),
    .pin6(n74193_1_pin6));  // open: pin1, pin7, pin15, pin14, pin13, pin12, pin11, pin10, pin9
  and and_1 (and_1_out, ballgoup, clock_1_out);
  and and_2 (and_2_out, ballgodown, clock_1_out);
  not not_1 (n74193_1_pin5, and_1_out);
  not not_2 (n74193_1_pin4, and_2_out);
  not not_3 (ballbit0, n74138_1_pin7);
  not not_4 (ballbit1, n74138_1_pin9);
  not not_5 (ballbit2, n74138_1_pin10);
  not not_6 (ballbit3, n74138_1_pin11);
  _74138 #(.ShowInternalStructure("true")) u_74138_1 (
    .pin1(n74193_1_pin3), .pin2(n74193_1_pin2), .pin3(n74193_1_pin6), .pin4(n74138_1_pin4),
    .pin5(n74138_1_pin5), .pin6(n74138_1_pin6), .pin7(n74138_1_pin7), .pin15(n74138_1_pin15),
    .pin14(n74138_1_pin14), .pin13(n74138_1_pin13), .pin12(n74138_1_pin12), .pin11(n74138_1_pin11),
    .pin10(n74138_1_pin10), .pin9(n74138_1_pin9));
  not not_7 (ballbit7, n74138_1_pin15);
  not not_8 (ballbit4, n74138_1_pin12);
  not not_9 (ballbit5, n74138_1_pin13);
  not not_10 (ballbit6, n74138_1_pin14);
  nor nor_1 (nor_1_out, BallHitLeft, nor_2_out);
  nor nor_2 (nor_2_out, nor_1_out, BallHitRight);
  LED led_1 (.in(ballbit0));
  LED led_2 (.in(ballbit1));
  LED led_3 (.in(ballbit2));
  LED led_4 (.in(ballbit3));
  LED led_5 (.in(ballbit4));
  LED led_6 (.in(ballbit5));
  LED led_7 (.in(ballbit6));
  LED led_8 (.in(ballbit7));
  _74244 #(.ShowInternalStructure("true")) u_74244_1 (
    .pin1(nor_2_out), .pin3(n74244_1_pin3), .pin5(n74244_1_pin5), .pin6(in_20), .pin7(n74244_1_pin7),
    .pin8(in_18), .pin9(n74244_1_pin9), .pin19(nor_1_out), .pin17(in_1), .pin15(in_3),
    .pin14(n74244_1_pin14), .pin13(in_5), .pin12(n74244_1_pin12), .pin11(in_7));  // open: pin2, pin4, pin18, pin16
  not not_11 (not_11_out, n74244_2_pin9);
  not not_12 (not_12_out, n74244_1_pin12);
  LED led_9 (.in(in_3));
  LED led_10 (.in(in_5));
  LED led_11 (.in(in_7));
  LED led_12 (.in(in_9));
  LED led_13 (.in(in_11));
  LED led_14 (.in(in_13));
  LED led_15 (.in(in_15));
  LED led_16 (.in(in_17));
  _74244 #(.ShowInternalStructure("true")) u_74244_2 (
    .pin1(nor_2_out), .pin2(in_16), .pin3(n74244_2_pin3), .pin4(in_14), .pin5(n74244_2_pin5), .pin6(in_12),
    .pin7(n74244_2_pin7), .pin8(in_10), .pin9(n74244_2_pin9), .pin19(nor_1_out), .pin18(n74244_2_pin9),
    .pin17(in_9), .pin16(n74244_2_pin7), .pin15(in_11), .pin14(n74244_2_pin5), .pin13(in_13),
    .pin12(n74244_2_pin3), .pin11(in_15));
  not not_13 (not_13_out, n74244_1_pin5);
  not not_14 (not_14_out, n74244_1_pin7);
  not not_15 (not_15_out, n74244_1_pin9);
  not not_16 (not_16_out, n74244_2_pin3);
  not not_17 (not_17_out, n74244_2_pin5);
  and and_3 (END4, not_17_out, ballbit4);
  not not_18 (not_18_out, n74244_2_pin7);
  and and_4 (END5, not_18_out, ballbit5);
  and and_5 (END6, not_11_out, ballbit6);
  and and_6 (END7, not_12_out, ballbit7);
  Clock clock_2 (.out(clock_2_out));
  LED led_17 (.in(a));
  LED led_18 (.in(b));
  LED led_19 (.in(c));
  LED led_20 (.in(k));
  LED led_21 (.in(l));
  LED led_22 (.in(m));
  LED led_23 (.in(u));
  LED led_24 (.in(v));
  LED led_25 (.in(w));
  LED led_26 (.in(ae));
  LED led_27 (.in(af));
  LED led_28 (.in(ag));
  LED led_29 (.in(ao));
  LED led_30 (.in(ap));
  LED led_31 (.in(aq));
  LED led_32 (.in(ay));
  LED led_33 (.in(az));
  LED led_34 (.in(ba));
  LED led_35 (.in(bi));
  LED led_36 (.in(bj));
  LED led_37 (.in(bk));
  LED led_38 (.in(bs));
  LED led_39 (.in(bt));
  LED led_40 (.in(bu));
  and and_7 (END0, not_13_out, ballbit0);
  and and_8 (END1, not_14_out, ballbit1);
  and and_9 (END2, not_15_out, ballbit2);
  and and_10 (END3, not_16_out, ballbit3);
  and and_11 (and_11_out, nor_4_out, clock_2_out);
  and and_12 (and_12_out, nor_3_out, clock_2_out);
  LED led_41 (.in(a1));
  LED led_42 (.in(b1));
  LED led_43 (.in(c1));
  LED led_44 (.in(d1));
  LED led_45 (.in(d));
  LED led_46 (.in(e));
  LED led_47 (.in(f));
  LED led_48 (.in(g));
  LED led_49 (.in(n));
  LED led_50 (.in(o));
  LED led_51 (.in(p));
  LED led_52 (.in(q));
  LED led_53 (.in(x));
  LED led_54 (.in(y));
  LED led_55 (.in(z));
  LED led_56 (.in(aa));
  LED led_57 (.in(ah));
  LED led_58 (.in(ai));
  LED led_59 (.in(aj));
  LED led_60 (.in(ak));
  LED led_61 (.in(ar));
  LED led_62 (.in(as));
  LED led_63 (.in(at));
  LED led_64 (.in(au));
  LED led_65 (.in(bb));
  LED led_66 (.in(bc));
  LED led_67 (.in(bd));
  LED led_68 (.in(be));
  LED led_69 (.in(bl));
  LED led_70 (.in(bm));
  LED led_71 (.in(bn));
  LED led_72 (.in(bo));
  LED led_73 (.in(bv));
  LED led_74 (.in(bw));
  LED led_75 (.in(bx));
  LED led_76 (.in(by));
  _74193 #(.ShowInternalStructure("true")) u_74193_2 (
    .pin2(n74193_2_pin2), .pin3(n74193_2_pin3), .pin4(n74193_2_pin4), .pin5(n74193_2_pin5),
    .pin6(n74193_2_pin6), .pin7(n74193_2_pin7));  // open: pin1, pin15, pin14, pin13, pin12, pin11, pin10, pin9
  not not_19 (n74193_2_pin5, and_11_out);
  not not_20 (n74193_2_pin4, and_12_out);
  _7442 #(.ShowInternalStructure("true")) u_7442_1 (
    .pin1(a1), .pin2(b1), .pin3(c1), .pin4(d1), .pin5(e1), .pin6(f1), .pin7(g1), .pin15(n74193_2_pin3),
    .pin14(n74193_2_pin2), .pin13(n74193_2_pin6), .pin12(n74193_2_pin7), .pin11(j1), .pin10(i1), .pin9(h1));
  not not_21 (BallHitLeft, a1);
  LED led_77 (.in(e1));
  LED led_78 (.in(f1));
  LED led_79 (.in(g1));
  LED led_80 (.in(h1));
  LED led_81 (.in(h));
  LED led_82 (.in(i));
  LED led_83 (.in(j));
  LED led_84 (.in(in_4));
  LED led_85 (.in(r));
  LED led_86 (.in(s));
  LED led_87 (.in(t));
  LED led_88 (.in(in_6));
  LED led_89 (.in(ab));
  LED led_90 (.in(ac));
  LED led_91 (.in(ad));
  LED led_92 (.in(in_8));
  LED led_93 (.in(al));
  LED led_94 (.in(am));
  LED led_95 (.in(an));
  LED led_96 (.in(in_10));
  LED led_97 (.in(av));
  LED led_98 (.in(aw));
  LED led_99 (.in(ax));
  LED led_100 (.in(in_12));
  LED led_101 (.in(bf));
  LED led_102 (.in(bg));
  LED led_103 (.in(bh));
  LED led_104 (.in(in_14));
  LED led_105 (.in(bp));
  LED led_106 (.in(bq));
  LED led_107 (.in(br));
  LED led_108 (.in(in_16));
  LED led_109 (.in(bz));
  LED led_110 (.in(ca));
  LED led_111 (.in(cb));
  LED led_112 (.in(in_18));
  _74244 #(.ShowInternalStructure("true")) u_74244_3 (
    .pin1(nor_2_out), .pin2(in_8), .pin3(n74244_1_pin12), .pin4(in_6), .pin5(n74244_1_pin14), .pin6(in_4),
    .pin8(in_2), .pin19(nor_1_out), .pin18(n74244_1_pin9), .pin17(in_17), .pin16(n74244_1_pin7),
    .pin15(in_19), .pin14(n74244_1_pin5), .pin12(n74244_1_pin3));  // open: pin7, pin9, pin13, pin11
  not not_22 (not_22_out, END5);
  not not_23 (not_23_out, END6);
  not not_24 (not_24_out, END7);
  LED led_113 (.in(i1));
  LED led_114 (.in(j1));
  not not_25 (not_25_out, END0);
  not not_26 (not_26_out, END1);
  not not_27 (not_27_out, END2);
  not not_28 (not_28_out, END3);
  and and_13 (Collision3, not_28_out, ballbit3);
  not not_29 (not_29_out, END4);
  and and_14 (Collision4, not_29_out, ballbit4);
  and and_15 (Collision5, not_22_out, ballbit5);
  and and_16 (Collision6, not_23_out, ballbit6);
  and and_17 (Collision7, not_24_out, ballbit7);
  and and_18 (Collision0, not_25_out, ballbit0);
  and and_19 (Collision1, not_26_out, ballbit1);
  and and_20 (Collision2, not_27_out, ballbit2);
  nor nor_3 (nor_3_out, BallHitLeft, nor_4_out);
  and and_21 (and_21_out, Collision1, n74244_1_pin5);
  and and_22 (and_22_out, Collision2, n74244_1_pin7);
  and and_23 (and_23_out, Collision3, n74244_1_pin9);
  and and_24 (and_24_out, Collision4, n74244_2_pin3);
  and and_25 (and_25_out, Collision5, n74244_2_pin5);
  and and_26 (and_26_out, Collision6, n74244_2_pin7);
  and and_27 (and_27_out, Collision7, n74244_2_pin9);
  nor nor_4 (nor_4_out, nor_3_out, BallHitRight);
  not not_30 (BallHitRight, j1);
  and and_28 (and_28_out, Collision0, n74244_1_pin3);
  _7485 #(.ShowInternalStructure("true")) u_7485_1 ();  // open: pin1, pin2, pin3, pin4, pin5, pin6, pin7, pin15, pin14, pin13, pin12, pin11, pin10, pin9
  xor xor_1 (xor_1_out, Collision1, and_21_out);
  xor xor_2 (xor_2_out, Collision2, and_22_out);
  xor xor_3 (xor_3_out, Collision3, and_23_out);
  xor xor_4 (xor_4_out, Collision4, and_24_out);
  xor xor_5 (xor_5_out, Collision5, and_25_out);
  xor xor_6 (xor_6_out, Collision6, and_26_out);
  xor xor_7 (xor_7_out, Collision7, and_27_out);
  xor xor_8 (xor_8_out, Collision0, and_28_out);
  and and_29 (CountUP3, xor_3_out, n74244_2_pin5);
  and and_30 (CountOFF3, n74244_2_pin5, and_23_out);
  and and_31 (CountUP4, xor_4_out, n74244_2_pin7);
  and and_32 (CountOFF4, n74244_2_pin7, and_24_out);
  and and_33 (CountUP5, xor_5_out, n74244_2_pin9);
  and and_34 (CountOFF5, n74244_2_pin9, and_25_out);
  and and_35 (CountUP6, xor_6_out, n74244_1_pin12);
  and and_36 (CountOFF6, n74244_1_pin12, and_26_out);
  and and_37 (CountUP7, xor_7_out, n74244_1_pin14);
  and and_38 (CountOFF7, n74244_1_pin14, and_27_out);
  and and_39 (CountUP0, xor_8_out, n74244_1_pin7);
  and and_40 (CountOFF0, n74244_1_pin7, and_28_out);
  and and_41 (CountUP1, xor_1_out, n74244_1_pin9);
  and and_42 (CountOFF1, n74244_1_pin9, and_21_out);
  and and_43 (CountUP2, xor_2_out, n74244_2_pin3);
  and and_44 (CountOFF2, n74244_2_pin3, and_22_out);
  xor xor_9 (CountDOWN0, CountOFF0, and_28_out);
  xor xor_10 (CountDOWN1, CountOFF1, and_21_out);
  xor xor_11 (CountDOWN2, CountOFF2, and_22_out);
  xor xor_12 (CountDOWN3, CountOFF3, and_23_out);
  xor xor_13 (CountDOWN4, CountOFF4, and_24_out);
  xor xor_14 (CountDOWN5, CountOFF5, and_25_out);
  xor xor_15 (CountDOWN6, CountOFF6, and_26_out);
  xor xor_16 (CountDOWN7, CountOFF7, and_27_out);
  LED led_115 (.in(P1_HIT));
  and and_45 (P1_HIT, BallHitLeft, unchecked_Collision);
  LED led_116 (.in(nor_5_out));
  nor nor_5 (nor_5_out, P1_HIT, P2_HIT);
  not not_31 (PaddleInflictedChange, nor_5_out);
  LED led_117 (.in(P2_HIT));
  and and_46 (P2_HIT, BallHitRight, unchecked_Collision);
  nor nor_6 (nor_6_out, PaddleInflictedChange, nor_7_out);
  nor nor_7 (nor_7_out, nor_6_out, GridInflictedChange);
  LED led_118 (.in(nor_8_out));
  nor nor_8 (nor_8_out, ballbit7, ballbit0);
  and and_47 (and_47_out, PaddleTop, not_34_out);
  not not_32 (GridInflictedChange, nor_8_out);
  not not_33 (not_33_out, nor_7_out);
  nor nor_9 (PaddleInflictedDOWN, and_47_out, PaddleInflictedUP);
  not not_34 (not_34_out, clock_3_out);
  Clock clock_3 (.out(clock_3_out));
  and and_48 (and_48_out, not_33_out, nor_6_out);
  not not_35 (not_35_out, and_48_out);
  nor nor_10 (PaddleInflictedUP, PaddleInflictedDOWN, and_49_out);
  and and_49 (and_49_out, not_34_out, PaddleBottom);
  _74244 #(.ShowInternalStructure("true")) u_74244_4 (
    .pin1(nor_6_out), .pin3(ballgoup), .pin5(ballgodown), .pin6(n74244_4_pin6), .pin8(n74244_4_pin8),
    .pin19(not_35_out), .pin17(GridInflictedUP), .pin15(GridInflictedDOWN), .pin14(ballgodown),
    .pin12(ballgoup));  // open: pin2, pin4, pin7, pin9, pin18, pin16, pin13, pin11
  and and_50 (PaddleInflictedOFF, nor_11_out, unchecked_countOFF);
  nor nor_11 (nor_11_out, PaddleBottom, PaddleTop);
  xor xor_17 (xor_17_out, P2_HIT, P1_HIT);
  and and_51 (PaddleTop, xor_17_out, unchecked_countUP);
  and and_52 (PaddleBottom, xor_17_out, unchecked_DOWN);
  _74244 #(.ShowInternalStructure("true")) u_74244_5 (
    .pin1(n74244_5_pin1), .pin2(n74244_5_pin2), .pin3(n74244_4_pin8), .pin4(n74244_5_pin2),
    .pin5(n74244_4_pin6), .pin19(PaddleInflictedOFF), .pin18(n74244_4_pin8), .pin17(PaddleInflictedUP),
    .pin16(n74244_4_pin6), .pin15(PaddleInflictedDOWN));  // open: pin6, pin7, pin8, pin9, pin14, pin13, pin12, pin11
  not not_36 (n74244_5_pin1, PaddleInflictedOFF);
  Pull_Resistor pull_resistor_1 (.node(n74244_5_pin2));
  nor nor_12 (GridInflictedUP, ballbit0, GridInflictedDOWN);
  LED led_119 (.in(GUARANTEED_ENDGAME));
  and and_53 (GUARANTEED_ENDGAME, xor_18_out, unchecked_ENDGAME);
  xor xor_18 (xor_18_out, BallHitLeft, BallHitRight);
  nor nor_13 (GridInflictedDOWN, GridInflictedUP, ballbit7);
  LED led_120 (.in(unchecked_ENDGAME));
  or or_1 (unchecked_ENDGAME, END1, END2, END3, END4, END5, END6, END7, END0);
  LED led_121 (.in(unchecked_countUP));
  or or_2 (unchecked_countUP, CountUP0, CountUP1, CountUP2, CountUP3, CountUP4, CountUP5, CountUP6, CountUP7);
  not not_37 (not_37_out, a1);
  and and_54 (a, not_37_out, ballbit0);
  not not_38 (not_38_out, a1);
  and and_55 (ao, not_38_out, ballbit4);
  not not_39 (not_39_out, b1);
  not not_40 (not_40_out, c1);
  and and_56 (b, not_39_out, ballbit0);
  not not_41 (not_41_out, b1);
  and and_57 (ap, not_41_out, ballbit4);
  not not_42 (not_42_out, d1);
  and and_58 (c, not_40_out, ballbit0);
  not not_43 (not_43_out, c1);
  not not_44 (not_44_out, d1);
  and and_59 (aq, not_43_out, ballbit4);
  not not_45 (not_45_out, e1);
  and and_60 (d, not_42_out, ballbit0);
  and and_61 (e, not_45_out, ballbit0);
  not not_46 (not_46_out, e1);
  and and_62 (ar, not_44_out, ballbit4);
  LED led_122 (.in(unchecked_countOFF));
  or or_3 (unchecked_countOFF, CountOFF1, CountOFF3, CountOFF4, CountOFF5, CountOFF6, CountOFF7, CountOFF2, CountOFF0);
  LED led_123 (.in(unchecked_DOWN));
  or or_4 (unchecked_DOWN, CountDOWN0, CountDOWN1, CountDOWN2, CountDOWN3, CountDOWN4, CountDOWN5, CountDOWN6, CountDOWN7);
  not not_47 (not_47_out, f1);
  and and_63 (f, not_47_out, ballbit0);
  not not_48 (not_48_out, f1);
  and and_64 (as, not_46_out, ballbit4);
  and and_65 (at, not_48_out, ballbit4);
  Pull_Resistor pull_resistor_2 (.node(unchecked_DOWN));
  not not_49 (not_49_out, g1);
  and and_66 (g, not_49_out, ballbit0);
  not not_50 (not_50_out, g1);
  and and_67 (au, not_50_out, ballbit4);
  not not_51 (not_51_out, h1);
  and and_68 (h, not_51_out, ballbit0);
  not not_52 (not_52_out, h1);
  and and_69 (av, not_52_out, ballbit4);
  not not_53 (not_53_out, i1);
  and and_70 (i, not_53_out, ballbit0);
  not not_54 (not_54_out, i1);
  and and_71 (aw, not_54_out, ballbit4);
  not not_55 (not_55_out, j1);
  and and_72 (j, not_55_out, ballbit0);
  not not_56 (not_56_out, j1);
  and and_73 (ax, not_56_out, ballbit4);
  LED led_124 (.in(unchecked_Collision));
  or or_5 (unchecked_Collision, Collision0, Collision1, Collision2, Collision3, Collision4, Collision5, Collision6, Collision7);
  Pull_Resistor pull_resistor_3 (.node(unchecked_Collision));
  not not_57 (not_57_out, a1);
  and and_74 (k, not_57_out, ballbit1);
  not not_58 (not_58_out, a1);
  and and_75 (ay, not_58_out, ballbit5);
  not not_59 (not_59_out, b1);
  not not_60 (not_60_out, c1);
  and and_76 (l, not_59_out, ballbit1);
  not not_61 (not_61_out, b1);
  and and_77 (az, not_61_out, ballbit5);
  not not_62 (not_62_out, d1);
  and and_78 (m, not_60_out, ballbit1);
  not not_63 (not_63_out, c1);
  not not_64 (not_64_out, d1);
  and and_79 (ba, not_63_out, ballbit5);
  not not_65 (not_65_out, e1);
  and and_80 (n, not_62_out, ballbit1);
  and and_81 (o, not_65_out, ballbit1);
  not not_66 (not_66_out, e1);
  and and_82 (bb, not_64_out, ballbit5);
  not not_67 (not_67_out, f1);
  and and_83 (p, not_67_out, ballbit1);
  not not_68 (not_68_out, f1);
  and and_84 (bc, not_66_out, ballbit5);
  and and_85 (bd, not_68_out, ballbit5);
  not not_69 (not_69_out, g1);
  and and_86 (q, not_69_out, ballbit1);
  not not_70 (not_70_out, g1);
  and and_87 (be, not_70_out, ballbit5);
  not not_71 (not_71_out, h1);
  and and_88 (r, not_71_out, ballbit1);
  not not_72 (not_72_out, h1);
  and and_89 (bf, not_72_out, ballbit5);
  not not_73 (not_73_out, i1);
  and and_90 (s, not_73_out, ballbit1);
  not not_74 (not_74_out, i1);
  and and_91 (bg, not_74_out, ballbit5);
  not not_75 (not_75_out, j1);
  and and_92 (t, not_75_out, ballbit1);
  not not_76 (not_76_out, j1);
  and and_93 (bh, not_76_out, ballbit5);
  not not_77 (not_77_out, a1);
  not not_78 (not_78_out, b1);
  and and_94 (u, not_77_out, ballbit2);
  not not_79 (not_79_out, a1);
  and and_95 (bi, not_79_out, ballbit6);
  not not_80 (not_80_out, c1);
  and and_96 (v, not_78_out, ballbit2);
  not not_81 (not_81_out, b1);
  not not_82 (not_82_out, c1);
  and and_97 (bj, not_81_out, ballbit6);
  not not_83 (not_83_out, d1);
  and and_98 (w, not_80_out, ballbit2);
  and and_99 (x, not_83_out, ballbit2);
  not not_84 (not_84_out, d1);
  and and_100 (bk, not_82_out, ballbit6);
  not not_85 (not_85_out, e1);
  and and_101 (y, not_85_out, ballbit2);
  not not_86 (not_86_out, e1);
  and and_102 (bl, not_84_out, ballbit6);
  and and_103 (bm, not_86_out, ballbit6);
  not not_87 (not_87_out, f1);
  and and_104 (z, not_87_out, ballbit2);
  not not_88 (not_88_out, f1);
  and and_105 (bn, not_88_out, ballbit6);
  not not_89 (not_89_out, g1);
  and and_106 (aa, not_89_out, ballbit2);
  not not_90 (not_90_out, g1);
  and and_107 (bo, not_90_out, ballbit6);
  not not_91 (not_91_out, h1);
  and and_108 (ab, not_91_out, ballbit2);
  not not_92 (not_92_out, h1);
  and and_109 (bp, not_92_out, ballbit6);
  not not_93 (not_93_out, i1);
  not not_94 (not_94_out, j1);
  and and_110 (ac, not_93_out, ballbit2);
  not not_95 (not_95_out, i1);
  and and_111 (bq, not_95_out, ballbit6);
  and and_112 (ad, not_94_out, ballbit2);
  not not_96 (not_96_out, j1);
  and and_113 (br, not_96_out, ballbit6);
  not not_97 (not_97_out, a1);
  not not_98 (not_98_out, b1);
  and and_114 (ae, not_97_out, ballbit3);
  not not_99 (not_99_out, a1);
  and and_115 (bs, not_99_out, ballbit7);
  not not_100 (not_100_out, c1);
  and and_116 (af, not_98_out, ballbit3);
  not not_101 (not_101_out, b1);
  not not_102 (not_102_out, c1);
  and and_117 (bt, not_101_out, ballbit7);
  not not_103 (not_103_out, d1);
  and and_118 (ag, not_100_out, ballbit3);
  and and_119 (ah, not_103_out, ballbit3);
  not not_104 (not_104_out, d1);
  and and_120 (bu, not_102_out, ballbit7);
  not not_105 (not_105_out, e1);
  and and_121 (ai, not_105_out, ballbit3);
  not not_106 (not_106_out, e1);
  and and_122 (bv, not_104_out, ballbit7);
  and and_123 (bw, not_106_out, ballbit7);
  not not_107 (not_107_out, f1);
  and and_124 (aj, not_107_out, ballbit3);
  not not_108 (not_108_out, f1);
  and and_125 (bx, not_108_out, ballbit7);
  not not_109 (not_109_out, g1);
  and and_126 (ak, not_109_out, ballbit3);
  not not_110 (not_110_out, g1);
  and and_127 (by, not_110_out, ballbit7);
  not not_111 (not_111_out, h1);
  and and_128 (al, not_111_out, ballbit3);
  not not_112 (not_112_out, h1);
  and and_129 (bz, not_112_out, ballbit7);
  not not_113 (not_113_out, i1);
  not not_114 (not_114_out, j1);
  and and_130 (am, not_113_out, ballbit3);
  not not_115 (not_115_out, i1);
  and and_131 (ca, not_115_out, ballbit7);
  and and_132 (an, not_114_out, ballbit3);
  not not_116 (not_116_out, j1);
  and and_133 (cb, not_116_out, ballbit7);
  // also tied to GND on the sheet: {n74138_1_pin5, n74138_1_pin4}
  // also tied to VCC on the sheet: n74138_1_pin6

  // Other names for the same wires on the sheet: ballhitbottom = ballbit7; ballhittop = ballbit0

  // Notes on the sheet:
  //   in_14: initial=0x1
  //   in_16: initial=0x1
  //   in_18: initial=0x1
  //   in_13: initial=0x1
  //   in_15: initial=0x1
  //   in_17: initial=0x1
endmodule
